// Logisim project Control_Unit.circ as structural Verilog
module Zero_Decoder (
  input  [5:0] Func_Code,
  output [3:0] ALU_SEL,
  output ALU_Unsigned
);

  ALU_Sel_Dec alu_sel_dec_1 (
    .f0(Func_Code[0]), .f1(Func_Code[1]), .f2(Func_Code[2]), .f3(Func_Code[3]), .f4(Func_Code[4]),
    .f5(Func_Code[5]), .AS0(ALU_SEL[0]), .AS1(ALU_SEL[1]), .AS2(ALU_SEL[2]), .AS4(ALU_SEL[3]),
    .\unsigned (ALU_Unsigned));
endmodule

module ALU_Sel_Dec (
  input  f0,
  input  f1,
  input  f2,
  input  f3,
  input  f4,
  input  f5,
  output AS0,
  output AS1,
  output AS2,
  output AS4,
  output \unsigned 
);

  wire \and , div, divu, lt, ltu, mul, mulu, \nor , \or , sub, \xor ;

  and and_1 (sub, ~f0, f1, ~f2, ~f3, ~f4, f5);  // AND_Gate
  and and_2 (mul, ~f0, ~f1, ~f2, f3, f4, ~f5);  // AND_Gate
  and and_3 (mulu, f0, ~f1, ~f2, f3, f4, ~f5);  // AND_Gate
  and and_4 (div, ~f0, f1, ~f2, f3, f4, ~f5);  // AND_Gate
  and and_5 (divu, f0, f1, ~f2, f3, f4, ~f5);  // AND_Gate
  and and_6 (\and , ~f0, ~f1, f2, ~f3, ~f4, f5);  // AND_Gate
  and and_7 (\or , f0, ~f1, f2, ~f3, ~f4, f5);  // AND_Gate
  and and_8 (\nor , f0, f1, f2, ~f3, ~f4, f5);  // AND_Gate
  and and_9 (\xor , ~f0, ~f1, ~f2, f3, ~f4, f5);  // AND_Gate
  and and_10 (lt, ~f0, f1, ~f2, f3, ~f4, f5);  // AND_Gate
  and and_11 (ltu, f0, f1, ~f2, f3, ~f4, f5);  // AND_Gate
  or or_1 (AS0, sub, div, divu, \or , \xor , ltu);
  or or_2 (AS1, mul, mulu, div, divu, \nor , \xor );
  or or_3 (AS2, \and , \or , \nor , \xor );
  or or_4 (AS4, lt, ltu);
  or or_5 (\unsigned , mulu, divu);
endmodule
